# Fritzing sketch Diyagram_Fritzing (saved by Fritzing 0.8.7b)
breadboards: 1

parts:
  U1 = NodeMCU V3.0 [part_number="Lolin v0.1"]
  Part1 = RFID USB Reader
  LED1 = RGB LED - (4 legs) [package="5 mm [THT]"]
  S1 = Pushbutton [package="[THT]"]
  J1 = Basic Servo
  R1 = Resistor [tolerance=±5% resistance=10k package=THT]

nets:
  N1: U1.D0, S1.Pin_1, S1.Pin_2, R1.Pin_0
  N2: U1.D2, Part1.GND
  N3: U1.D3, LED1.red_cathode
  N4: U1.D4, Part1.GNDT
  N5: U1.D5, Part1.CP
  N6: U1.D6, Part1.ANT1
  N7: U1.D7, Part1.ANT2
  N8: U1.D8, LED1.green_cathode
  GND: U1.GND, Part1.TX-O, J1.gnd, R1.Pin_1
  VCC: U1.3V3, Part1.VCC, S1.Pin_3, S1.Pin_4, J1.vcc

custom parts:
  NodeMCU V3.0: ESP8266 based NodeMCU
